// Logisim project Test.circ as structural Verilog: 8 circuits, main circuit main
module main (
);

  wire and_1_out, clock_1_out, Control_Unit_asrc, Control_Unit_brn, Control_Unit_jmp, Control_Unit_m2r,
       Control_Unit_mr, Control_Unit_mw, Control_Unit_rdst, main_1_p4, n32_register_file_1_p5,
       n32_register_file_1_p6, not_1_out, or_1_out;
  wire [1:0] Control_Unit_alu_op;
  wire [2:0] main_1_p3;
  wire [3:0] PC_31_28_out_2;
  wire [4:0] multiplexer_1_out, Splitter_out_3, Splitter_out_4, Splitter_out_5;
  wire [5:0] Splitter_out_6, Splitter_out_7;
  wire [15:0] Splitter_out_8;
  wire [23:0] S_J_2_out_2, S_J_out_2, shifter_1_out, shifter_4_out;
  wire [25:0] Splitter_out_2;
  wire [27:0] bit_extender_1_out, shifter_2_out;
  wire [31:0] adder_1_out, adder_2_out, bit_extender_2_out, INS_28_0__PC_31_28_out_3, main_1_p5,
       multiplexer_2_out, multiplexer_3_out, multiplexer_4_out, n32_register_file_1_p4,
       n32_register_file_1_p7, PC_q, ram_1_data, rom_1_data, shifter_3_out;

  Clock clock_1 (.out(clock_1_out));
  Register #(.width(32)) PC (.D(multiplexer_4_out), .Q(PC_q), .clk(clock_1_out));  // open: en, clr
  Splitter_for_Mems S_J (.in_1(PC_q), .out_2(S_J_out_2));
  Adder #(.width(32)) adder_1 (.a(PC_q), .b(32'h4), .out(adder_1_out));  // open: cin, cout
  Shifter #(.width(24), .shift("lr")) shifter_1 (.in(S_J_out_2), .\dist (5'b00010), .out(shifter_1_out));
  ROM #(.addrWidth(24), .dataWidth(32)) rom_1 (.addr(shifter_1_out), .data(rom_1_data));  // open: sel
  assign bit_extender_1_out = {{2{Splitter_out_2[25]}}, Splitter_out_2};  // Bit_Extender bit_extender_1
  Splitter_Reg Splitter (
    .in_1(rom_1_data), .out_7(Splitter_out_7), .out_6(Splitter_out_6), .out_2(Splitter_out_2),
    .out_3(Splitter_out_3), .out_4(Splitter_out_4), .out_5(Splitter_out_5), .out_8(Splitter_out_8));
  Shifter #(.width(28)) shifter_2 (.in(bit_extender_1_out), .\dist (5'b00010), .out(shifter_2_out));
  Multiplexer #(.width(5), .enable("false")) multiplexer_1 (
    .in0(Splitter_out_4), .in1(Splitter_out_5), .out(multiplexer_1_out), .sel(Control_Unit_rdst));
  Spliier_PC PC_31_28 (.in_1(adder_1_out), .out_2(PC_31_28_out_2));
  Shifter #(.width(32)) shifter_3 (.in(bit_extender_2_out), .\dist (5'b00010), .out(shifter_3_out));
  // _32_register_file 32_register_file_1: pin names not known; wires that end beside it: Splitter_out_3, Splitter_out_4, multiplexer_1_out, n32_register_file_1_p4, n32_register_file_1_p5, n32_register_file_1_p6, n32_register_file_1_p7
  assign bit_extender_2_out = {{16{Splitter_out_8[15]}}, Splitter_out_8};  // Bit_Extender bit_extender_2
  Join_PC INS_28_0__PC_31_28 (.in_1(shifter_2_out), .in_2(PC_31_28_out_2), .out_3(INS_28_0__PC_31_28_out_3));
  Multiplexer #(.width(32), .enable("false")) multiplexer_2 (
    .in0(n32_register_file_1_p7), .in1(bit_extender_2_out), .out(multiplexer_2_out), .sel(Control_Unit_asrc));
  Multiplexer #(.width(32), .enable("false")) multiplexer_3 (
    .in0(adder_1_out), .in1(adder_2_out), .out(multiplexer_3_out), .sel(and_1_out));
  Adder #(.width(32)) adder_2 (.a(adder_1_out), .b(shifter_3_out), .out(adder_2_out));  // open: cin, cout
  and and_1 (and_1_out, main_1_p4, Control_Unit_brn);
  // ALU_main main_1: pin names not known; wires that end beside it: n32_register_file_1_p6, multiplexer_2_out, main_1_p3, main_1_p4, main_1_p5
  ALU_Cont alu_cont_1 (.OPC(Control_Unit_alu_op), .FUN(Splitter_out_7), .out_3(main_1_p3));
  Multiplexer #(.width(32), .enable("false")) multiplexer_4 (
    .in0(INS_28_0__PC_31_28_out_3), .in1(multiplexer_3_out), .out(multiplexer_4_out), .sel(not_1_out));
  not not_1 (not_1_out, Control_Unit_jmp);
  Splitter_for_Mems S_J_2 (.in_1(main_1_p5), .out_2(S_J_2_out_2));
  Control_Unit Control_Unit (
    .in_1(Splitter_out_6), .RDST(Control_Unit_rdst), .RW(n32_register_file_1_p5), .ASRC(Control_Unit_asrc),
    .MW(Control_Unit_mw), .MR(Control_Unit_mr), .M2R(Control_Unit_m2r), .BRN(Control_Unit_brn),
    .JMP(Control_Unit_jmp), .ALU_op(Control_Unit_alu_op));
  Shifter #(.width(24), .shift("lr")) shifter_4 (.in(S_J_2_out_2), .\dist (5'b00010), .out(shifter_4_out));
  or or_1 (or_1_out, Control_Unit_mw, Control_Unit_mr);
  RAM #(.addrWidth(24), .dataWidth(32), .bus("separate")) ram_1 (
    .addr(shifter_4_out), .din(n32_register_file_1_p7), .data(ram_1_data), .str(Control_Unit_mw),
    .sel(or_1_out), .clk(clock_1_out), .ld(Control_Unit_mr));  // open: clr
  Multiplexer #(.width(32), .enable("false")) multiplexer_5 (
    .in0(ram_1_data), .in1(main_1_p5), .out(n32_register_file_1_p4), .sel(Control_Unit_m2r));

  // Notes on the sheet:
  //   IM
  //   contents of rom_1 (hex, n*v repeats v):
  //   8c010000 8c020004 221820 ac030008 8000000
  //   Rdst
  //   RF
  //   ASrc
  //   PSrc
  //   JMP
  //   ALU
  //   M2R
endmodule

module Splitter_Reg (
  input  [31:0] in_1,
  output [25:0] out_2,
  output [4:0] out_3,
  output [4:0] out_4,
  output [4:0] out_5,
  output [5:0] out_6,
  output [5:0] out_7,
  output [15:0] out_8
);


  assign out_2 = in_1[25:0];
  assign out_3 = in_1[25:21];
  assign out_4 = in_1[20:16];
  assign out_5 = in_1[15:11];
  assign out_6 = in_1[31:26];
  assign out_7 = in_1[5:0];
  assign out_8 = in_1[15:0];
endmodule

module Spliier_PC (
  input  [31:0] in_1,
  output [3:0] out_2
);


  assign out_2 = in_1[31:28];
endmodule

module Join_PC (
  input  [27:0] in_1,
  input  [3:0] in_2,
  output [31:0] out_3
);


  assign out_3 = {in_2, in_1};
endmodule

module Splitter_for_Mems (
  input  [31:0] in_1,
  output [23:0] out_2
);


  assign out_2 = in_1[23:0];
endmodule

module Control_Unit (
  input  [5:0] in_1,
  output RDST,
  output RW,
  output ASRC,
  output MW,
  output MR,
  output M2R,
  output BRN,
  output JMP,
  output [1:0] ALU_op
);

  wire and_3_out, and_4_out, not_1_out, not_2_out, not_3_out, not_4_out, not_5_out, not_6_out, not_7_out,
       not_8_out, not_9_out, not_10_out;

  not not_1 (not_1_out, in_1[3]);
  not not_2 (not_2_out, in_1[1]);
  not not_3 (not_3_out, in_1[2]);
  not not_4 (not_4_out, in_1[1]);
  not not_5 (not_5_out, in_1[3]);
  or or_1 (ASRC, in_1[1], in_1[3]);
  and and_1 (MW, in_1[5], in_1[3]);
  not not_6 (not_6_out, in_1[3]);
  not not_7 (not_7_out, in_1[0]);
  not not_8 (not_8_out, in_1[3]);
  not not_9 (not_9_out, in_1[2]);
  not not_10 (not_10_out, in_1[1]);
  and and_2 (RDST, not_1_out, not_2_out);
  and and_3 (and_3_out, not_3_out, not_4_out);
  or or_2 (RW, and_3_out, and_4_out);
  and and_4 (and_4_out, in_1[5], not_5_out);
  and and_5 (MR, in_1[5], not_6_out);
  and and_6 (JMP, in_1[1], not_7_out);
  and and_7 (ALU_op[1], not_8_out, not_9_out, not_10_out);

  assign ALU_op[0] = in_1[2];
  assign BRN = in_1[2];
  assign M2R = in_1[1];
endmodule

module ALU_Cont (
  input  [1:0] OPC,
  input  [5:0] FUN,
  output [2:0] out_3
);

  wire and_1_out, and_2_out, and_3_out, and_4_out, not_1_out, not_2_out, not_3_out;

  not not_1 (not_1_out, FUN[5]);
  not not_2 (not_2_out, OPC[1]);
  not not_3 (not_3_out, FUN[2]);
  and and_1 (and_1_out, OPC[1], FUN[0]);
  and and_2 (and_2_out, OPC[1], FUN[3]);
  and and_3 (and_3_out, OPC[1], not_1_out);
  and and_4 (and_4_out, OPC[1], FUN[1]);
  or or_1 (out_3[1], not_2_out, not_3_out);
  or or_2 (out_3[0], and_1_out, and_2_out);
  or or_3 (out_3[2], OPC[0], and_3_out, and_4_out);
endmodule

module HA (
  input  a,
  input  b,
  output sum,
  output carry
);

  and and_1 (sum, a, b);
  xor xor_1 (carry, a, b);
endmodule
